// Logisim project BA101V32I_32b_single_cycle_cpu.circ as structural Verilog: 10 circuits, main circuit main
module main (
  input  in_1
);

  wire clk, reset;
  wire [31:0] dmem_addr, dmem_din, dmem_dout, gpu_1_screen0, gpu_1_screen1, gpu_1_screen2, gpu_1_screen3,
       gpu_1_screen4, gpu_1_screen5, gpu_1_screen6, gpu_1_screen7, imem_addr, imem_dout, mem_info;

  Clock clock_1 (.out(clk));
  POR #(.PorHighDuration(1)) por_1 (.out(reset));
  CPU cpu_1 (
    .debug(in_1), .clk(clk), .reset(reset), .imem_dout(imem_dout), .dmem_dout(dmem_dout),
    .mem_info(mem_info), .imem_addr(imem_addr), .dmem_addr(dmem_addr), .dmem_din(dmem_din));
  MEM mem_1 (
    .debug(in_1), .clk(clk), .reset(reset), .mem_info(mem_info), .imem_addr(imem_addr),
    .dmem_addr(dmem_addr), .dmem_din(dmem_din), .imem_dout(imem_dout), .dmem_dout(dmem_dout));
  // Probe on imem_addr
  // Probe on imem_addr
  // Probe on imem_dout
  // Probe on imem_dout
  // Probe on dmem_addr
  // Probe on dmem_addr
  GPU gpu_1 (
    .deug(in_1), .clk(clk), .reset(reset), .mem_info(mem_info), .dmem_addr(dmem_addr), .dmem_din(dmem_din),
    .screen0(gpu_1_screen0), .screen1(gpu_1_screen1), .screen2(gpu_1_screen2), .screen3(gpu_1_screen3),
    .screen4(gpu_1_screen4), .screen5(gpu_1_screen5), .screen6(gpu_1_screen6), .screen7(gpu_1_screen7));
  // Probe on dmem_dout
  // Probe on dmem_dout
  DotMatrix #(.inputtype("row"), .matrixcols(16), .matrixrows(16)) dotmatrix_1 (
    .row0(gpu_1_screen0[31:16]), .row1(gpu_1_screen0[15:0]), .row2(gpu_1_screen1[31:16]),
    .row3(gpu_1_screen1[15:0]), .row4(gpu_1_screen2[31:16]), .row5(gpu_1_screen2[15:0]),
    .row6(gpu_1_screen3[31:16]), .row7(gpu_1_screen3[15:0]), .row8(gpu_1_screen4[31:16]),
    .row9(gpu_1_screen4[15:0]), .row10(gpu_1_screen5[31:16]), .row11(gpu_1_screen5[15:0]),
    .row12(gpu_1_screen6[31:16]), .row13(gpu_1_screen6[15:0]), .row14(gpu_1_screen7[31:16]),
    .row15(gpu_1_screen7[15:0]));
  // Probe on dmem_din
  // Probe on dmem_din

  // Other names for the same wires on the sheet: debug = in_1
endmodule

module CPU (
  input  debug,
  input  clk,
  input  reset,
  input  [31:0] imem_dout,
  input  [31:0] dmem_dout,
  output [31:0] mem_info,
  output [31:0] imem_addr,
  output [31:0] dmem_addr,
  output [31:0] dmem_din
);

  wire clk_t, clock_1_out;
  wire [5:0] cmp_res;
  wire [31:0] alu_info, aluop_res, id_info, if_info, if_info_out, imm, rs1_data, wb_data, wb_info;

  Clock clock_1 (.out(clock_1_out));
  Multiplexer #(.enable("false")) multiplexer_1 (.in0(clock_1_out), .in1(clk), .out(clk_t), .sel(debug));
  CPU_IF cpu_if_1 (
    .debug(debug), .clk(clk_t), .reset(reset), .if_info(if_info_out), .inst(imem_dout), .pc_next(aluop_res),
    .pc(imem_addr));
  CPU_ID cpu_id_1 (
    .debug(debug), .clk(clk_t), .reset(reset), .id_info_in(id_info), .pc(imem_addr), .inst(imem_dout),
    .wb_data(wb_data), .imm(imm), .if_info(if_info), .id_info_out(id_info), .alu_info(alu_info),
    .mem_info(mem_info), .wb_info(wb_info), .rs1_data(rs1_data), .rs2_data(dmem_din));
  CPU_EX cpu_ex_1 (
    .debug(debug), .clk(clk_t), .reset(reset), .alu_info(alu_info), .pc(imem_addr), .rs1(rs1_data),
    .rs2(dmem_din), .imm(imm), .aluop_res(aluop_res), .cmp_res(cmp_res));
  CPU_MEM cpu_mem_1 (
    .debug(debug), .clk(clk_t), .reset(reset), .dmem_dout(dmem_dout), .if_info_in(if_info),
    .aluop_res(aluop_res), .cmp_res(cmp_res), .dmem_addr(dmem_addr), .dmem_din(dmem_din),
    .if_info_out(if_info_out));
  CPU_WB cpu_wb_1 (
    .debug(debug), .clk(clk_t), .reset(reset), .wb_info(wb_info), .pc(imem_addr), .aluop_res(aluop_res),
    .dmem_dout(dmem_dout), .wb_data(wb_data));

  // Other names for the same wires on the sheet: rs2_data[31:0] = dmem_din
endmodule

module CPU_IF (
  input  debug,
  input  clk,
  input  reset,
  input  [31:0] if_info,
  input  [31:0] inst,
  input  [31:0] pc_next,
  output [31:0] pc
);

  wire clk_t, clock_1_out, pc_src_sel;
  wire [31:0] multiplexer_2_out, pc_incre;

  Clock clock_1 (.out(clock_1_out));
  Multiplexer #(.enable("false")) multiplexer_1 (.in0(clock_1_out), .in1(clk), .out(clk_t), .sel(debug));
  Adder #(.width(32)) adder_1 (.a(pc), .b(32'h4), .out(pc_incre));  // open: cin, cout
  or or_1 (pc_src_sel, if_info[6], if_info[7]);
  Register #(.width(32)) pc_reg (.D(multiplexer_2_out), .en(1'b1), .clk(clk_t), .Q(pc), .clr(reset));
  Multiplexer #(.width(32), .enable("false")) multiplexer_2 (
    .in0(pc_incre), .in1(pc_next), .out(multiplexer_2_out), .sel(pc_src_sel));
endmodule

module CPU_ID (
  input  debug,
  input  clk,
  input  reset,
  input  [31:0] id_info_in,
  input  [31:0] pc,
  input  [31:0] inst,
  input  [31:0] wb_data,
  output [31:0] imm,
  output [31:0] if_info,
  output [31:0] id_info_out,
  output [31:0] alu_info,
  output [31:0] mem_info,
  output [31:0] wb_info,
  output [31:0] rs1_data,
  output [31:0] rs2_data
);

  wire and_53_out, and_57_out, and_59_out, and_60_out, and_61_out, and_65_out, and_66_out, and_67_out,
       and_68_out, and_69_out, and_70_out, and_73_out, and_74_out, and_75_out, and_76_out, and_77_out,
       and_79_out, and_80_out, and_81_out, and_82_out, clk_t, clock_1_out, comparator_1_eq, comparator_2_eq,
       funct3_000, funct3_001, funct3_010, funct3_011, funct3_100, funct3_101, funct3_110, funct3_111,
       funct7_0000000, funct7_0000001, funct7_0100000, opcode_4_2_000, opcode_4_2_001, opcode_4_2_010,
       opcode_4_2_011, opcode_4_2_100, opcode_4_2_101, opcode_4_2_110, opcode_4_2_111, opcode_6_5_00,
       opcode_6_5_01, opcode_6_5_10, opcode_6_5_11, or_14_out, rv32_add, rv32_addi, rv32_and, rv32_andi,
       rv32_auipc, rv32_branch, rv32_ebreak, rv32_ecall, rv32_imm_sel_i, rv32_imm_sel_j, rv32_imm_sel_u,
       rv32_jalr, rv32_op, rv32_op_32, rv32_op_imm, rv32_op_imm_32, rv32_or, rv32_ori, rv32_sll, rv32_slli,
       rv32_slt, rv32_slti, rv32_sltiu, rv32_sltu, rv32_sra, rv32_srai, rv32_srl, rv32_srli, rv32_system,
       rv32_xor, rv32_xori;
  wire [31:0] b_imm, i_imm, j_imm, s_imm;

  Clock clock_1 (.out(clock_1_out));
  Multiplexer #(.enable("false")) multiplexer_1 (.in0(clock_1_out), .in1(clk), .out(clk_t), .sel(debug));
  Pull_Resistor pull_resistor_1 (.node(if_info));
  Pull_Resistor pull_resistor_2 (.node(id_info_out));
  Pull_Resistor pull_resistor_3 (.node(alu_info));
  Pull_Resistor pull_resistor_4 (.node(mem_info));
  Pull_Resistor pull_resistor_5 (.node(wb_info));
  or or_1 (if_info[7], rv32_imm_sel_j, rv32_jalr);
  and and_1 (if_info[0], rv32_branch, funct3_000);
  and and_2 (if_info[1], rv32_branch, funct3_001);
  and and_3 (if_info[2], rv32_branch, funct3_100);
  and and_4 (if_info[3], rv32_branch, funct3_101);
  and and_5 (if_info[4], rv32_branch, funct3_110);
  and and_6 (if_info[5], rv32_branch, funct3_111);
  CPU_ID_REGFILE cpu_id_regfile_1 (
    .debug(debug), .clk(clk_t), .reset(reset), .regfile_info(id_info_in), .rs1_sel(inst[19:15]),
    .rs2_sel(inst[24:20]), .rd_sel(inst[11:7]), .rd_data(wb_data), .rs1_data(rs1_data), .rs2_data(rs2_data));
  and and_7 (opcode_4_2_000, ~inst[2], ~inst[3], ~inst[4]);  // AND_Gate
  and and_8 (opcode_4_2_001, inst[2], ~inst[3], ~inst[4]);  // AND_Gate
  and and_9 (opcode_4_2_010, ~inst[2], inst[3], ~inst[4]);  // AND_Gate
  and and_10 (opcode_4_2_011, inst[2], inst[3], ~inst[4]);  // AND_Gate
  and and_11 (opcode_4_2_100, ~inst[2], ~inst[3], inst[4]);  // AND_Gate
  and and_12 (opcode_4_2_101, inst[2], ~inst[3], inst[4]);  // AND_Gate
  and and_13 (opcode_4_2_110, ~inst[2], inst[3], inst[4]);  // AND_Gate
  and and_14 (opcode_4_2_111, inst[2], inst[3], inst[4]);
  and and_15 (opcode_6_5_00, ~inst[5], ~inst[6]);  // AND_Gate
  and and_16 (opcode_6_5_01, inst[5], ~inst[6]);  // AND_Gate
  and and_17 (opcode_6_5_10, ~inst[5], inst[6]);  // AND_Gate
  and and_18 (opcode_6_5_11, inst[5], inst[6]);
  Comparator #(.width(12)) comparator_1 (.a(inst[31:20]), .b({12{1'b0}}), .eq(comparator_1_eq));  // open: gt, lt
  Comparator #(.width(12)) comparator_2 (.a(inst[31:20]), .b(12'h1), .eq(comparator_2_eq));  // open: gt, lt
  and and_19 (rv32_ecall, rv32_system, funct3_000, comparator_1_eq);
  and and_20 (rv32_ebreak, rv32_system, funct3_000, comparator_2_eq);
  and and_21 (funct3_000, ~inst[12], ~inst[13], ~inst[14]);  // AND_Gate
  and and_22 (funct3_001, inst[12], ~inst[13], ~inst[14]);  // AND_Gate
  and and_23 (funct3_010, ~inst[12], inst[13], ~inst[14]);  // AND_Gate
  and and_24 (funct3_011, inst[12], inst[13], ~inst[14]);  // AND_Gate
  and and_25 (funct3_100, ~inst[12], ~inst[13], inst[14]);  // AND_Gate
  and and_26 (funct3_101, inst[12], ~inst[13], inst[14]);  // AND_Gate
  and and_27 (funct3_110, ~inst[12], inst[13], inst[14]);  // AND_Gate
  and and_28 (funct3_111, inst[12], inst[13], inst[14]);
  and and_29 (rv32_addi, rv32_op_imm, funct3_000);
  and and_30 (rv32_slli, rv32_op_imm, funct3_001, funct7_0000000);
  and and_31 (rv32_slti, rv32_op_imm, funct3_010);
  and and_32 (rv32_sltiu, rv32_op_imm, funct3_011);
  and and_33 (rv32_xori, rv32_op_imm, funct3_100);
  and and_34 (rv32_srli, rv32_op_imm, funct3_101, funct7_0000000);
  and and_35 (rv32_srai, rv32_op_imm, funct3_101, funct7_0100000);
  and and_36 (rv32_ori, rv32_op_imm, funct3_110);
  and and_37 (rv32_andi, rv32_op_imm, funct3_111);
  and and_38 (funct7_0000000, ~inst[25], ~inst[26], ~inst[27], ~inst[28], ~inst[29], ~inst[30], ~inst[31]);  // AND_Gate
  and and_39 (funct7_0000001, inst[25], ~inst[26], ~inst[27], ~inst[28], ~inst[29], ~inst[30], ~inst[31]);  // AND_Gate
  and and_40 (funct7_0100000, ~inst[25], ~inst[26], ~inst[27], ~inst[28], ~inst[29], inst[30], ~inst[31]);  // AND_Gate
  and and_41 (rv32_add, rv32_op, funct3_000, funct7_0000000);
  and and_42 (alu_info[3], rv32_op, funct3_000, funct7_0100000);
  and and_43 (rv32_sll, rv32_op, funct3_001, funct7_0000000);
  and and_44 (rv32_slt, rv32_op, funct3_010, funct7_0000000);
  and and_45 (rv32_sltu, rv32_op, funct3_011, funct7_0000000);
  and and_46 (rv32_xor, rv32_op, funct3_100, funct7_0000000);
  and and_47 (rv32_srl, rv32_op, funct3_101, funct7_0000000);
  and and_48 (rv32_sra, rv32_op, funct3_101, funct7_0100000);
  and and_49 (rv32_or, rv32_op, funct3_110, funct7_0000000);
  and and_50 (rv32_and, rv32_op, funct3_111, funct7_0000000);
  and and_51 (wb_info[0], opcode_4_2_000, opcode_6_5_00);
  and and_52 (mem_info[0], opcode_4_2_000, opcode_6_5_01);
  and and_53 (and_53_out, opcode_4_2_000, opcode_6_5_10);
  and and_54 (rv32_branch, opcode_4_2_000, opcode_6_5_11);
  and and_55 (rv32_op_imm, opcode_4_2_100, opcode_6_5_00);
  and and_56 (rv32_op, opcode_4_2_100, opcode_6_5_01);
  and and_57 (and_57_out, opcode_4_2_100, opcode_6_5_10);
  and and_58 (rv32_system, opcode_4_2_100, opcode_6_5_11);
  assign i_imm = {{20{inst[31]}}, inst[31:20]};  // Bit_Extender bit_extender_1
  assign s_imm = {{20{inst[31]}}, {inst[31:25], inst[11:7]}};  // Bit_Extender bit_extender_2
  assign b_imm = {{19{inst[31]}}, {inst[31], inst[7], inst[30:25], inst[11:8], 1'b0}};  // Bit_Extender bit_extender_3
  assign j_imm = {{11{inst[31]}}, {inst[31], inst[19:12], inst[20], inst[30:21], 1'b0}};  // Bit_Extender bit_extender_4
  or or_2 (rv32_imm_sel_i, wb_info[0], rv32_op_imm, rv32_jalr);
  or or_3 (rv32_imm_sel_u, alu_info[12], rv32_auipc);
  assign imm = rv32_imm_sel_i ? i_imm : 32'bz;  // Controlled_Buffer controlled_buffer_1
  assign imm = mem_info[0] ? s_imm : 32'bz;  // Controlled_Buffer controlled_buffer_2
  assign imm = rv32_branch ? b_imm : 32'bz;  // Controlled_Buffer controlled_buffer_3
  assign imm = rv32_imm_sel_u ? {inst[31:12], {12{1'b0}}} : 32'bz;  // Controlled_Buffer controlled_buffer_4
  assign imm = rv32_imm_sel_j ? j_imm : 32'bz;  // Controlled_Buffer controlled_buffer_5
  and and_59 (and_59_out, opcode_4_2_001, opcode_6_5_00);
  and and_60 (and_60_out, opcode_4_2_001, opcode_6_5_01);
  and and_61 (and_61_out, opcode_4_2_001, opcode_6_5_10);
  and and_62 (rv32_jalr, opcode_4_2_001, opcode_6_5_11);
  and and_63 (rv32_auipc, opcode_4_2_101, opcode_6_5_00);
  and and_64 (alu_info[12], opcode_4_2_101, opcode_6_5_01);
  and and_65 (and_65_out, opcode_4_2_101, opcode_6_5_10);
  and and_66 (and_66_out, opcode_4_2_101, opcode_6_5_11);
  or or_4 (alu_info[4], rv32_sll, rv32_slli);
  or or_5 (alu_info[5], rv32_slt, rv32_slti);
  or or_6 (alu_info[6], rv32_sltu, rv32_sltiu);
  or or_7 (alu_info[7], rv32_xor, rv32_xori);
  or or_8 (alu_info[8], rv32_srl, rv32_srli);
  or or_9 (alu_info[9], rv32_sra, rv32_srai);
  or or_10 (alu_info[10], rv32_or, rv32_ori);
  or or_11 (alu_info[11], rv32_and, rv32_andi);
  or or_12 (alu_info[0], rv32_auipc, rv32_imm_sel_j, rv32_jalr);
  or or_13 (alu_info[2], rv32_add, rv32_addi, rv32_auipc, wb_info[0], mem_info[0], rv32_imm_sel_j, rv32_jalr);
  and and_67 (and_67_out, opcode_4_2_010, opcode_6_5_00);
  and and_68 (and_68_out, opcode_4_2_010, opcode_6_5_01);
  and and_69 (and_69_out, opcode_4_2_010, opcode_6_5_10);
  and and_70 (and_70_out, opcode_4_2_010, opcode_6_5_11);
  and and_71 (rv32_op_imm_32, opcode_4_2_110, opcode_6_5_00);
  and and_72 (rv32_op_32, opcode_4_2_110, opcode_6_5_01);
  and and_73 (and_73_out, opcode_4_2_110, opcode_6_5_10);
  and and_74 (and_74_out, opcode_4_2_110, opcode_6_5_11);
  or or_14 (or_14_out, rv32_branch, mem_info[0], rv32_ecall, rv32_ebreak);
  or or_15 (alu_info[1], rv32_imm_sel_i, mem_info[0], rv32_branch, rv32_imm_sel_u, rv32_imm_sel_j);
  not not_1 (id_info_out[0], or_14_out);
  and and_75 (and_75_out, opcode_4_2_011, opcode_6_5_00);
  and and_76 (and_76_out, opcode_4_2_011, opcode_6_5_01);
  and and_77 (and_77_out, opcode_4_2_011, opcode_6_5_10);
  and and_78 (rv32_imm_sel_j, opcode_4_2_011, opcode_6_5_11);
  and and_79 (and_79_out, opcode_4_2_111, opcode_6_5_00);
  and and_80 (and_80_out, opcode_4_2_111, opcode_6_5_01);
  and and_81 (and_81_out, opcode_4_2_111, opcode_6_5_10);
  and and_82 (and_82_out, opcode_4_2_111, opcode_6_5_11);

  // Other names for the same wires on the sheet: rd[4:0] = inst[11:7]; rs2[4:0] = inst[24:20];
  //   u_imm[31:12] = inst[31:12]; funct7[6:0] = inst[31:25]; funct3[2:0] = inst[14:12]; rs1[4:0] = inst[19:15];
  //   alu_a_sel = alu_info[0]; alu_b_sel = alu_info[1]; need_imm = alu_info[1]; alu_add = alu_info[2];
  //   alu_sub = alu_info[3]; rv32_sub = alu_info[3]; alu_sll = alu_info[4]; alu_slt = alu_info[5];
  //   alu_sltu = alu_info[6]; alu_xor = alu_info[7]; alu_srl = alu_info[8]; alu_sra = alu_info[9];
  //   alu_or = alu_info[10]; alu_and = alu_info[11]; alu_lui = alu_info[12]; rv32_lui = alu_info[12];
  //   need_rd = id_info_out[0]; rv32_beq = if_info[0]; rv32_bne = if_info[1]; rv32_blt = if_info[2];
  //   rv32_bgt = if_info[3]; rv32_bltu = if_info[4]; rv32_bgtu = if_info[5]; opcode[6:0] = inst[6:0];
  //   dmem_we = mem_info[0]; rv32_imm_sel_s = mem_info[0]; rv32_store = mem_info[0]; rv32_imm_sel_b = rv32_branch;
  //   rv32_jal = rv32_imm_sel_j; regfile_wb_sel = wb_info[0]; rv32_load = wb_info[0]
endmodule

module CPU_ID_REGFILE (
  input  debug,
  input  clk,
  input  reset,
  input  [31:0] regfile_info,
  input  [4:0] rs1_sel,
  input  [4:0] rs2_sel,
  input  [4:0] rd_sel,
  input  [31:0] rd_data,
  output [31:0] rs1_data,
  output [31:0] rs2_data
);

  wire clk_t, clock_1_out, reg_en_0, reg_en_1, reg_en_2, reg_en_3, reg_en_4, reg_en_5, reg_en_6, reg_en_7,
       reg_en_8, reg_en_9, reg_en_10, reg_en_11, reg_en_12, reg_en_13, reg_en_14, reg_en_15, reg_en_16,
       reg_en_17, reg_en_18, reg_en_19, reg_en_20, reg_en_21, reg_en_22, reg_en_23, reg_en_24, reg_en_25,
       reg_en_26, reg_en_27, reg_en_28, reg_en_29, reg_en_30, reg_en_31;
  wire [31:0] reg1, reg2, reg3, reg4, reg5, reg6, reg7, reg8, reg9, reg10, reg11, reg12, reg13, reg14, reg15,
       reg16, reg17, reg18, reg19, reg20, reg21, reg22, reg23, reg24, reg25, reg26, reg27, reg28, reg29,
       reg30, reg31;

  Clock clock_1 (.out(clock_1_out));
  Multiplexer #(.enable("false")) multiplexer_1 (.in0(clock_1_out), .in1(clk), .out(clk_t), .sel(debug));
  Decoder #(.select(5)) decoder_1 (
    .out0(reg_en_0), .out1(reg_en_1), .out2(reg_en_2), .out3(reg_en_3), .out4(reg_en_4), .out5(reg_en_5),
    .out6(reg_en_6), .out7(reg_en_7), .out8(reg_en_8), .out9(reg_en_9), .out10(reg_en_10), .out11(reg_en_11),
    .out12(reg_en_12), .out13(reg_en_13), .out14(reg_en_14), .out15(reg_en_15), .out16(reg_en_16),
    .out17(reg_en_17), .out18(reg_en_18), .out19(reg_en_19), .out20(reg_en_20), .out21(reg_en_21),
    .out22(reg_en_22), .out23(reg_en_23), .out24(reg_en_24), .out25(reg_en_25), .out26(reg_en_26),
    .out27(reg_en_27), .out28(reg_en_28), .out29(reg_en_29), .out30(reg_en_30), .out31(reg_en_31),
    .sel(rd_sel), .en(regfile_info[0]));
  Multiplexer #(.select(5), .width(32), .enable("false")) multiplexer_2 (
    .in0({32{1'b0}}), .in1(reg1), .in2(reg2), .in3(reg3), .in4(reg4), .in5(reg5), .in6(reg6), .in7(reg7),
    .in8(reg8), .in9(reg9), .in10(reg10), .in11(reg11), .in12(reg12), .in13(reg13), .in14(reg14),
    .in15(reg15), .in16(reg16), .in17(reg17), .in18(reg18), .in19(reg19), .in20(reg20), .in21(reg21),
    .in22(reg22), .in23(reg23), .in24(reg24), .in25(reg25), .in26(reg26), .in27(reg27), .in28(reg28),
    .in29(reg29), .in30(reg30), .in31(reg31), .out(rs1_data), .sel(rs1_sel));
  Multiplexer #(.select(5), .width(32), .enable("false")) multiplexer_3 (
    .in0({32{1'b0}}), .in1(reg1), .in2(reg2), .in3(reg3), .in4(reg4), .in5(reg5), .in6(reg6), .in7(reg7),
    .in8(reg8), .in9(reg9), .in10(reg10), .in11(reg11), .in12(reg12), .in13(reg13), .in14(reg14),
    .in15(reg15), .in16(reg16), .in17(reg17), .in18(reg18), .in19(reg19), .in20(reg20), .in21(reg21),
    .in22(reg22), .in23(reg23), .in24(reg24), .in25(reg25), .in26(reg26), .in27(reg27), .in28(reg28),
    .in29(reg29), .in30(reg30), .in31(reg31), .out(rs2_data), .sel(rs2_sel));
  Register #(.width(32)) register_1 (.D(rd_data), .en(reg_en_1), .clk(clk_t), .Q(reg1), .clr(reset));
  Register #(.width(32)) register_2 (.D(rd_data), .en(reg_en_2), .clk(clk_t), .Q(reg2), .clr(reset));
  Register #(.width(32)) register_3 (.D(rd_data), .en(reg_en_3), .clk(clk_t), .Q(reg3), .clr(reset));
  Register #(.width(32)) register_4 (.D(rd_data), .en(reg_en_4), .clk(clk_t), .Q(reg4), .clr(reset));
  Register #(.width(32)) register_5 (.D(rd_data), .en(reg_en_5), .clk(clk_t), .Q(reg5), .clr(reset));
  Register #(.width(32)) register_6 (.D(rd_data), .en(reg_en_6), .clk(clk_t), .Q(reg6), .clr(reset));
  Register #(.width(32)) register_7 (.D(rd_data), .en(reg_en_7), .clk(clk_t), .Q(reg7), .clr(reset));
  Register #(.width(32)) register_8 (.D(rd_data), .en(reg_en_8), .clk(clk_t), .Q(reg8), .clr(reset));
  Register #(.width(32)) register_9 (.D(rd_data), .en(reg_en_9), .clk(clk_t), .Q(reg9), .clr(reset));
  Register #(.width(32)) register_10 (.D(rd_data), .en(reg_en_10), .clk(clk_t), .Q(reg10), .clr(reset));
  Register #(.width(32)) register_11 (.D(rd_data), .en(reg_en_11), .clk(clk_t), .Q(reg11), .clr(reset));
  Register #(.width(32)) register_12 (.D(rd_data), .en(reg_en_12), .clk(clk_t), .Q(reg12), .clr(reset));
  Register #(.width(32)) register_13 (.D(rd_data), .en(reg_en_13), .clk(clk_t), .Q(reg13), .clr(reset));
  Register #(.width(32)) register_14 (.D(rd_data), .en(reg_en_14), .clk(clk_t), .Q(reg14), .clr(reset));
  Register #(.width(32)) register_15 (.D(rd_data), .en(reg_en_15), .clk(clk_t), .Q(reg15), .clr(reset));
  Register #(.width(32)) register_16 (.D(rd_data), .en(reg_en_16), .clk(clk_t), .Q(reg16), .clr(reset));
  Register #(.width(32)) register_17 (.D(rd_data), .en(reg_en_17), .clk(clk_t), .Q(reg17), .clr(reset));
  Register #(.width(32)) register_18 (.D(rd_data), .en(reg_en_18), .clk(clk_t), .Q(reg18), .clr(reset));
  Register #(.width(32)) register_19 (.D(rd_data), .en(reg_en_19), .clk(clk_t), .Q(reg19), .clr(reset));
  Register #(.width(32)) register_20 (.D(rd_data), .en(reg_en_20), .clk(clk_t), .Q(reg20), .clr(reset));
  Register #(.width(32)) register_21 (.D(rd_data), .en(reg_en_21), .clk(clk_t), .Q(reg21), .clr(reset));
  Register #(.width(32)) register_22 (.D(rd_data), .en(reg_en_22), .clk(clk_t), .Q(reg22), .clr(reset));
  Register #(.width(32)) register_23 (.D(rd_data), .en(reg_en_23), .clk(clk_t), .Q(reg23), .clr(reset));
  Register #(.width(32)) register_24 (.D(rd_data), .en(reg_en_24), .clk(clk_t), .Q(reg24), .clr(reset));
  Register #(.width(32)) register_25 (.D(rd_data), .en(reg_en_25), .clk(clk_t), .Q(reg25), .clr(reset));
  Register #(.width(32)) register_26 (.D(rd_data), .en(reg_en_26), .clk(clk_t), .Q(reg26), .clr(reset));
  Register #(.width(32)) register_27 (.D(rd_data), .en(reg_en_27), .clk(clk_t), .Q(reg27), .clr(reset));
  Register #(.width(32)) register_28 (.D(rd_data), .en(reg_en_28), .clk(clk_t), .Q(reg28), .clr(reset));
  Register #(.width(32)) register_29 (.D(rd_data), .en(reg_en_29), .clk(clk_t), .Q(reg29), .clr(reset));
  Register #(.width(32)) register_30 (.D(rd_data), .en(reg_en_30), .clk(clk_t), .Q(reg30), .clr(reset));
  Register #(.width(32)) register_31 (.D(rd_data), .en(reg_en_31), .clk(clk_t), .Q(reg31), .clr(reset));

  // Other names for the same wires on the sheet: wb_en = regfile_info[0]
endmodule

module CPU_EX (
  input  debug,
  input  clk,
  input  reset,
  input  [31:0] alu_info,
  input  [31:0] pc,
  input  [31:0] rs1,
  input  [31:0] rs2,
  input  [31:0] imm,
  output [31:0] aluop_res,
  output [5:0] cmp_res
);

  wire clk_t, clock_1_out, comparator_3_lt, comparator_4_lt, or_2_out;
  wire [31:0] adder_1_out, and_1_out, bit_extender_1_out, bit_extender_2_out, controlled_buffer_1_out,
       input_a, input_b, or_1_out, shifter_1_out, shifter_2_out, shifter_3_out, xor_1_out;

  Clock clock_1 (.out(clock_1_out));
  Multiplexer #(.enable("false")) multiplexer_1 (.in0(clock_1_out), .in1(clk), .out(clk_t), .sel(debug));
  Pull_Resistor pull_resistor_1 (.node(alu_info));
  Comparator #(.width(32)) comparator_1 (.a(rs1), .b(rs2), .gt(cmp_res[3]), .eq(cmp_res[0]), .lt(cmp_res[2]));
  Comparator #(.width(32), .mode("unsigned")) comparator_2 (
    .a(rs1), .b(rs2), .gt(cmp_res[5]), .lt(cmp_res[4]));  // open: eq
  not not_1 (cmp_res[1], cmp_res[0]);
  Multiplexer #(.width(32), .enable("false")) multiplexer_2 (.in0(rs1), .in1(pc), .out(input_a), .sel(alu_info[0]));
  Multiplexer #(.width(32), .enable("false")) multiplexer_3 (.in0(rs2), .in1(imm), .out(input_b), .sel(alu_info[1]));
  assign controlled_buffer_1_out = alu_info[2] ? input_b : 32'bz;  // Controlled_Buffer controlled_buffer_1
  assign controlled_buffer_1_out = alu_info[3] ? ~input_b : 32'bz;  // Controlled_Inverter controlled_inverter_1
  Adder #(.width(32)) adder_1 (
    .a(input_a), .b(controlled_buffer_1_out), .out(adder_1_out), .cin(alu_info[3]));  // open: cout
  Shifter #(.width(32)) shifter_1 (.in(input_a), .\dist (input_b[4:0]), .out(shifter_1_out));
  Comparator #(.width(32)) comparator_3 (.a(input_a), .b(input_b), .lt(comparator_3_lt));  // open: gt, eq
  Comparator #(.width(32), .mode("unsigned")) comparator_4 (
    .a(input_a), .b(input_b), .lt(comparator_4_lt));  // open: gt, eq
  assign xor_1_out = input_a ^ input_b;  // XOR_Gate xor_1, 32 bits wide
  Shifter #(.width(32), .shift("lr")) shifter_2 (.in(input_a), .\dist (input_b[4:0]), .out(shifter_2_out));
  Shifter #(.width(32), .shift("ar")) shifter_3 (.in(input_a), .\dist (input_b[4:0]), .out(shifter_3_out));
  assign or_1_out = input_a | input_b;  // OR_Gate or_1, 32 bits wide
  assign and_1_out = input_a & input_b;  // AND_Gate and_1, 32 bits wide
  or or_2 (or_2_out, alu_info[2], alu_info[3]);
  assign aluop_res = or_2_out ? adder_1_out : 32'bz;  // Controlled_Buffer controlled_buffer_2
  assign aluop_res = alu_info[4] ? shifter_1_out : 32'bz;  // Controlled_Buffer controlled_buffer_3
  assign aluop_res = alu_info[5] ? bit_extender_1_out : 32'bz;  // Controlled_Buffer controlled_buffer_4
  assign bit_extender_1_out = {{31{1'b0}}, comparator_3_lt};  // Bit_Extender bit_extender_1
  assign aluop_res = alu_info[6] ? bit_extender_2_out : 32'bz;  // Controlled_Buffer controlled_buffer_5
  assign bit_extender_2_out = {{31{1'b0}}, comparator_4_lt};  // Bit_Extender bit_extender_2
  assign aluop_res = alu_info[7] ? xor_1_out : 32'bz;  // Controlled_Buffer controlled_buffer_6
  assign aluop_res = alu_info[8] ? shifter_2_out : 32'bz;  // Controlled_Buffer controlled_buffer_7
  assign aluop_res = alu_info[9] ? shifter_3_out : 32'bz;  // Controlled_Buffer controlled_buffer_8
  assign aluop_res = alu_info[10] ? or_1_out : 32'bz;  // Controlled_Buffer controlled_buffer_9
  assign aluop_res = alu_info[11] ? and_1_out : 32'bz;  // Controlled_Buffer controlled_buffer_10
  assign aluop_res = alu_info[12] ? input_b : 32'bz;  // Controlled_Buffer controlled_buffer_11

  // Other names for the same wires on the sheet: in_a_sel = alu_info[0]; in_b_sel = alu_info[1];
  //   alu_add = alu_info[2]; alu_sub = alu_info[3]; alu_sll = alu_info[4]; alu_slt = alu_info[5];
  //   alu_sltu = alu_info[6]; alu_xor = alu_info[7]; alu_srl = alu_info[8]; alu_sra = alu_info[9];
  //   alu_or = alu_info[10]; alu_and = alu_info[11]; alu_lui = alu_info[12]; alu_cmp_eq = alu_info[13];
  //   alu_cmp_ne = alu_info[14]; alu_cmp_lt = alu_info[15]; alu_cmp_gt = alu_info[16]; alu_cmp_ltu = alu_info[17];
  //   alu_cmp_gtu = alu_info[18]
endmodule

module CPU_MEM (
  input  debug,
  input  clk,
  input  reset,
  input  [31:0] dmem_dout,
  input  [31:0] if_info_in,
  input  [31:0] aluop_res,
  input  [5:0] cmp_res,
  output [31:0] dmem_addr,
  output [31:0] dmem_din,
  output [31:0] if_info_out
);

  wire beq_hit, bgt_hit, bgtu_hit, blt_hit, bltu_hit, bne_hit, clk_t, clock_1_out;

  Clock clock_1 (.out(clock_1_out));
  Multiplexer #(.enable("false")) multiplexer_1 (.in0(clock_1_out), .in1(clk), .out(clk_t), .sel(debug));
  and and_1 (beq_hit, if_info_in[0], cmp_res[0]);
  and and_2 (bne_hit, if_info_in[1], cmp_res[1]);
  and and_3 (blt_hit, if_info_in[2], cmp_res[2]);
  and and_4 (bgt_hit, if_info_in[3], cmp_res[3]);
  and and_5 (bltu_hit, if_info_in[4], cmp_res[4]);
  and and_6 (bgtu_hit, if_info_in[5], cmp_res[5]);
  or or_1 (if_info_out[6], beq_hit, bne_hit, blt_hit, bgt_hit, bltu_hit, bgtu_hit);

  assign dmem_addr = aluop_res;
  assign if_info_out[7] = if_info_in[7];

  // Other names for the same wires on the sheet: if_info[31:0] = {if_info_out[31:8], if_info_in[7], if_info_out[6:0]};
  //   pc_src_sel = if_info_out[6]
endmodule

module CPU_WB (
  input  debug,
  input  clk,
  input  reset,
  input  [31:0] wb_info,
  input  [31:0] pc,
  input  [31:0] aluop_res,
  input  [31:0] dmem_dout,
  output [31:0] wb_data
);

  wire clk_t, clock_1_out;

  Clock clock_1 (.out(clock_1_out));
  Multiplexer #(.enable("false")) multiplexer_1 (.in0(clock_1_out), .in1(clk), .out(clk_t), .sel(debug));
  Multiplexer #(.width(32), .enable("false")) multiplexer_2 (
    .in0(aluop_res), .in1(dmem_dout), .out(wb_data), .sel(wb_info[0]));

  // Other names for the same wires on the sheet: imem_dout[31:0] = dmem_dout; regfile_wb_sel = wb_info[0]
endmodule

module MEM (
  input  debug,
  input  clk,
  input  reset,
  input  [31:0] mem_info,
  input  [31:0] imem_addr,
  input  [31:0] dmem_addr,
  input  [31:0] dmem_din,
  output [31:0] imem_dout,
  output [31:0] dmem_dout
);

  wire and_1_out, clk_t, clock_1_out, comparator_1_lt;

  Clock clock_1 (.out(clock_1_out));
  Multiplexer #(.enable("false")) multiplexer_1 (.in0(clock_1_out), .in1(clk), .out(clk_t), .sel(debug));
  RAM #(.addrWidth(24), .dataWidth(32), .trigger("high")) IMEM (
    .addr(imem_addr[25:2]), .we(1'b0), .oe(1'b1), .data(imem_dout));
  Comparator #(.width(32), .mode("unsigned")) comparator_1 (
    .a(dmem_addr), .b(32'h2000000), .lt(comparator_1_lt));  // open: gt, eq
  and and_1 (and_1_out, mem_info[0], comparator_1_lt);
  RAM #(.addrWidth(24), .dataWidth(32), .trigger("falling"), .databus("bibus")) DMEM (
    .addr(dmem_addr[25:2]), .we(and_1_out), .oe(1'b1), .clk(clk_t), .din(dmem_din), .dout(dmem_dout));

  // Other names for the same wires on the sheet: dmem_we = mem_info[0]
endmodule

module GPU (
  input  deug,
  input  clk,
  input  reset,
  input  [31:0] mem_info,
  input  [31:0] dmem_addr,
  input  [31:0] dmem_din,
  output [31:0] screen0,
  output [31:0] screen1,
  output [31:0] screen2,
  output [31:0] screen3,
  output [31:0] screen4,
  output [31:0] screen5,
  output [31:0] screen6,
  output [31:0] screen7
);

  wire and_1_out, clk_t, clock_1_out, comparator_1_gt, decoder_1_out0, decoder_1_out1, decoder_1_out2,
       decoder_1_out3, decoder_1_out4, decoder_1_out5, decoder_1_out6, decoder_1_out7;

  Clock clock_1 (.out(clock_1_out));
  Multiplexer #(.enable("false")) multiplexer_1 (.in0(clock_1_out), .in1(clk), .out(clk_t), .sel(deug));
  Comparator #(.width(32), .mode("unsigned")) comparator_1 (
    .a(dmem_addr), .b(32'h1ffffff), .gt(comparator_1_gt));  // open: eq, lt
  Decoder #(.select(3)) decoder_1 (
    .out0(decoder_1_out0), .out1(decoder_1_out1), .out2(decoder_1_out2), .out3(decoder_1_out3),
    .out4(decoder_1_out4), .out5(decoder_1_out5), .out6(decoder_1_out6), .out7(decoder_1_out7),
    .sel(dmem_addr[4:2]), .en(and_1_out));
  and and_1 (and_1_out, mem_info[0], comparator_1_gt);
  Register #(.width(32)) register_1 (.D(dmem_din), .en(decoder_1_out0), .clk(clk_t), .Q(screen0));  // open: clr
  Register #(.width(32)) register_2 (.D(dmem_din), .en(decoder_1_out4), .clk(clk_t), .Q(screen4));  // open: clr
  Register #(.width(32)) register_3 (.D(dmem_din), .en(decoder_1_out1), .clk(clk_t), .Q(screen1));  // open: clr
  Register #(.width(32)) register_4 (.D(dmem_din), .en(decoder_1_out5), .clk(clk_t), .Q(screen5));  // open: clr
  Register #(.width(32)) register_5 (.D(dmem_din), .en(decoder_1_out2), .clk(clk_t), .Q(screen2));  // open: clr
  Register #(.width(32)) register_6 (.D(dmem_din), .en(decoder_1_out6), .clk(clk_t), .Q(screen6));  // open: clr
  Register #(.width(32)) register_7 (.D(dmem_din), .en(decoder_1_out3), .clk(clk_t), .Q(screen3));  // open: clr
  Register #(.width(32)) register_8 (.D(dmem_din), .en(decoder_1_out7), .clk(clk_t), .Q(screen7));  // open: clr

  // Other names for the same wires on the sheet: dmem_we = mem_info[0]
endmodule
